# Fritzing sketch Waterboy_sketch (saved by Fritzing 0.9.3b)

parts:
  Bauteil1 = HX711 Weighing Sensor Module
  Pro_Micro1 = Pro Micro
  IC1 = L293D [package=THT]
  M1 = DC Motor
  Load_Cell1 = Load Cell - Red/white/black/green
  BAT1 = BC9VPC [package=bc9vpc]

nets:
  VCC: Bauteil1.VCC, Pro_Micro1.VCC, IC1.Enable_1, IC1.+V
  N1: Bauteil1.GND, Pro_Micro1.GND#23, BAT1.V-
  N2: Bauteil1.DO/RX, Pro_Micro1.D14/MISO
  N3: Bauteil1.CK/TX, Pro_Micro1.D15/SCLK
  N4: Bauteil1.E+, Load_Cell1.wire1
  N5: Bauteil1.E-, Load_Cell1.wire3
  N6: Bauteil1.A+, Load_Cell1.wire4
  N7: Bauteil1.A-, Load_Cell1.wire2
  N8: Pro_Micro1.GND#4, IC1.0V
  N9: Pro_Micro1.D8, IC1.In_2
  N10: Pro_Micro1.D9, IC1.In_1
  N11: Pro_Micro1.RAW, IC1.+Vmotor, BAT1.V+
  N12: IC1.Out_1_(_Controlled_by_Enable_1_), M1.pin_2
  N13: IC1.Out_2_(_Controlled_by_Enable_1_), M1.pin_1

custom parts:
  Pro Micro: The SparkFun Pro Micro is a complete USB-based microcontoller development system, in a very small footprint, capable of implementing many types of projects. All programming can be done via the USB port.
  Load Cell - Red/white/black/green: A rectangle load cell/weighting pressure Sensor with four wires - Red, white, black, green. Normally corresponding with E+, E-, A+, A- respectively.
